// Logisim project cpu.circ as structural Verilog: 2 circuits, main circuit main
module main (
  input  [15:0] From_Instr_Mem,
  input  reset,
  input  clk,
  output [15:0] r0,
  output [15:0] r1,
  output [15:0] r2,
  output [15:0] r3,
  output [15:0] Display_0,
  output [15:0] Display_1,
  output [15:0] To_Instr_Mem,
  output [15:0] Data_Mem_Data,
  output [15:0] Data_Mem_Addr,
  output Data_Mem_Write
);

  wire ALUsrc, and_2_out, and_3_out, branch, branchNE, demultiplexer_1_out0, demultiplexer_1_out1, display,
       equal, jal, JR, jump, Kill, LUI, main_1_signed_overflow, MemToReg, multiplexer_5_out, not_1_out,
       not_2_out, or_2_out, RegWrite, signext;
  wire [1:0] multiplexer_2_out, RegDST;
  wire [3:0] ALUswitch;
  wire [5:0] funct;
  wire [7:6] Imm;
  wire [15:0] adder_1_out, adder_2_out, and_1_out, bit_extender_1_out, DataOut, ExImm, multiplexer_1_out,
       multiplexer_3_out, multiplexer_6_out, multiplexer_7_out, multiplexer_8_out, multiplexer_10_out, PC,
       ReadData0, shifter_1_out, SignExtImm, subtractor_1_out, TargetAdd, WriteData, ZeroExtImm;
  wire [15:8] instrP;

  Register #(.width(16)) u_PC (.D(PC), .Q(To_Instr_Mem), .clk(clk));  // open: en, clr
  Multiplexer #(.width(16)) multiplexer_1 (
    .in0(From_Instr_Mem), .in1(16'h6), .out(multiplexer_1_out), .sel(Kill));  // open: en
  Register #(.width(16)) register_1 (.D(multiplexer_1_out), .Q({instrP, Imm, funct}), .clk(clk));  // open: en, clr
  assign and_1_out = 16'hf000 & To_Instr_Mem;  // AND_Gate and_1, 16 bits wide
  assign bit_extender_1_out = {{4{1'b0}}, {instrP[11:8], Imm, funct}};  // Bit_Extender bit_extender_1
  assign TargetAdd = and_1_out | bit_extender_1_out;  // OR_Gate or_1, 16 bits wide
  Control control_1 (
    .Function(funct), .op3(instrP[15]), .op2(instrP[14]), .op1(instrP[13]), .op0(instrP[12]),
    .ALUSWITCH(ALUswitch), .RegDST0(RegDST[0]), .RegDST1(RegDST[1]), .Jump(jump), .Branch(branch),
    .MemToReg(MemToReg), .signext(signext), .MemWrite(Data_Mem_Write), .ALUSrc(ALUsrc), .RegWrite(RegWrite),
    .jr(JR), .Lui(LUI), .BranchNE(branchNE), .Jal(jal), .display(display));
  assign ZeroExtImm = {{8{1'b0}}, {Imm, funct}};  // Bit_Extender bit_extender_2
  assign SignExtImm = {{8{Imm[7]}}, {Imm, funct}};  // Bit_Extender bit_extender_3
  Multiplexer #(.select(2), .width(2)) multiplexer_2 (
    .in0(instrP[9:8]), .in1(Imm), .in3(2'b11), .out(multiplexer_2_out), .sel(RegDST));  // open: in2, en
  Regfile_main REGFILE (
    .Read_register_1(instrP[11:10]), .Read_register_2(instrP[9:8]), .write_register(multiplexer_2_out),
    .write_data(WriteData), .Reg_0_Value(r0), .Reg_1_Value(r1), .Reg_2_Value(r2), .Reg_3_Value(r3),
    .RegWrite(RegWrite), .clock(clk), .Read_Data_1(ReadData0), .Read_Data_2(Data_Mem_Data));
  Multiplexer #(.width(16)) multiplexer_3 (
    .in0(Data_Mem_Data), .in1(ExImm), .out(multiplexer_3_out), .sel(ALUsrc));  // open: en
  Multiplexer #(.width(16)) multiplexer_4 (.in0(ZeroExtImm), .in1(SignExtImm), .out(ExImm), .sel(signext));  // open: en
  Adder #(.width(16)) adder_1 (.a(To_Instr_Mem), .b(16'h1), .out(adder_1_out));  // open: cin, cout
  alu_main main_1 (
    .Switch__S(ALUswitch), .X(ReadData0), .Equal(equal), .RESULT(Data_Mem_Addr),
    .Signed_Overflow(main_1_signed_overflow), .Y(multiplexer_3_out));
  LED led_1 (.in(main_1_signed_overflow));
  Subtractor #(.width(16)) subtractor_1 (.a(adder_1_out), .b(16'h1), .out(subtractor_1_out));  // open: bin, bout
  and and_2 (and_2_out, branch, equal);
  and and_3 (and_3_out, branchNE, not_1_out);
  not not_1 (not_1_out, equal);
  Adder #(.width(16)) adder_2 (.a(subtractor_1_out), .b(ExImm), .out(adder_2_out));  // open: cin, cout
  or or_2 (or_2_out, and_2_out, and_3_out);
  assign DataOut = Data_Mem_Write ? Data_Mem_Data : 16'bz;  // Controlled_Buffer controlled_buffer_1
  Multiplexer multiplexer_5 (.in0(1'b0), .in1(1'b1), .out(multiplexer_5_out), .sel(display));  // open: en
  Multiplexer #(.width(16)) multiplexer_6 (
    .in0(adder_1_out), .in1(adder_2_out), .out(multiplexer_6_out), .sel(or_2_out));  // open: en
  RAM #(.addrWidth(16), .dataWidth(16)) ram_1 (
    .addr(Data_Mem_Addr), .data(DataOut), .sel(1'b1), .clk(clk), .ld(not_2_out), .clr(reset));
  not not_2 (not_2_out, Data_Mem_Write);
  Demultiplexer #(.enable("false")) demultiplexer_1 (
    .out0(demultiplexer_1_out0), .out1(demultiplexer_1_out1), .in(multiplexer_5_out), .sel(funct[0]));
  Multiplexer #(.width(16)) multiplexer_7 (
    .in0(multiplexer_6_out), .in1(TargetAdd), .out(multiplexer_7_out), .sel(jump));  // open: en
  Multiplexer #(.width(16)) multiplexer_8 (
    .in0(Data_Mem_Addr), .in1(DataOut), .out(multiplexer_8_out), .sel(MemToReg));  // open: en
  Register #(.width(16)) register_2 (.D(ReadData0), .en(demultiplexer_1_out0), .Q(Display_0), .clk(clk));  // open: clr
  or or_3 (Kill, jump, JR, or_2_out);
  Shifter #(.width(16)) shifter_1 (.in(ExImm), .\dist (4'b1000), .out(shifter_1_out));
  Register #(.width(16)) register_3 (.D(ReadData0), .en(demultiplexer_1_out1), .Q(Display_1), .clk(clk));  // open: clr
  Multiplexer #(.width(16)) multiplexer_9 (.in0(multiplexer_7_out), .in1(ReadData0), .out(PC), .sel(JR));  // open: en
  Multiplexer #(.width(16)) multiplexer_10 (
    .in0(multiplexer_8_out), .in1(shifter_1_out), .out(multiplexer_10_out), .sel(LUI));  // open: en
  Hex_Digit_Display hex_digit_display_1 (.value(Display_0[15:12]));  // open: dp
  Multiplexer #(.width(16)) multiplexer_11 (
    .in0(multiplexer_10_out), .in1(To_Instr_Mem), .out(WriteData), .sel(jal));  // open: en
  Hex_Digit_Display hex_digit_display_2 (.value(Display_0[7:4]));  // open: dp
  Hex_Digit_Display hex_digit_display_3 (.value(Display_0[11:8]));  // open: dp
  Hex_Digit_Display hex_digit_display_4 (.value(Display_0[3:0]));  // open: dp
  Hex_Digit_Display hex_digit_display_5 (.value(Display_1[11:8]));  // open: dp
  Hex_Digit_Display hex_digit_display_6 (.value(Display_1[15:12]));  // open: dp
  Hex_Digit_Display hex_digit_display_7 (.value(Display_1[3:0]));  // open: dp
  Hex_Digit_Display hex_digit_display_8 (.value(Display_1[7:4]));  // open: dp

  // Other names for the same wires on the sheet: Address[15:0] = Data_Mem_Addr; CurrPC[15:0] = To_Instr_Mem;
  //   d0[15:0] = Display_0; d1[15:0] = Display_1; Imm[5:0] = funct; instrP[7:0] = {Imm, funct};
  //   JumpAdd[11:0] = {instrP[11:8], Imm, funct}; rd[1:0] = Imm; instr[15:0] = From_Instr_Mem; rt[1:0] = instrP[9:8];
  //   rs[1:0] = instrP[11:10]; OpCode[3:0] = instrP[15:12]; MemWrite = Data_Mem_Write; DataIn[15:0] = Data_Mem_Data;
  //   ReadData1[15:0] = Data_Mem_Data

  // Notes on the sheet:
  //   This is the current PC that you need to send as OUTPUT
  //   This is the instruction that you would receive as INPUT
  //   This is a CLK that is an INPUT driven from the harness.
  //   Remember, this circuit is loaded from the harness to be tested!
  //   DO NOT CHANGE THE LOCATIONS OF THE INPUTS OR OUTPUTS! IF YOU DO SO, YOU NEED TO MAKE SURE THE PINS ARE IN THE RIGHT PLACES!
  //   These are OUTPUTS of the circuit
  //   These are OUTPUTS of the circuit
endmodule

module Control (
  input  op3,
  input  op2,
  input  op1,
  input  op0,
  input  [5:0] Function,
  output [3:0] ALUSWITCH,
  output RegDST0,
  output RegDST1,
  output Jump,
  output Branch,
  output MemToReg,
  output signext,
  output MemWrite,
  output ALUSrc,
  output RegWrite,
  output jr,
  output Lui,
  output BranchNE,
  output Jal,
  output display
);

  wire addi_out, and_1_out, andi_out, beq_out, bne_out, disp_out, j_out, jal_out, jr_out, lui_out, lw_out,
       not_1_out, not_2_out, not_3_out, not_4_out, ori_out;
  wire [1:0] ALUsel0_out;

  not not_1 (not_1_out, op3);
  not not_2 (not_2_out, op2);
  not not_3 (not_3_out, op0);
  not not_4 (not_4_out, op1);
  and and_1 (and_1_out, not_1_out, not_2_out, not_4_out, not_3_out);
  and u_jal (jal_out, not_1_out, not_2_out, not_4_out, op0);
  and j (j_out, not_1_out, not_2_out, op1, not_3_out);
  and u_jr (jr_out, not_1_out, not_2_out, op1, op0);
  and beq (beq_out, not_1_out, op2, not_4_out, not_3_out);
  and addi (addi_out, not_1_out, op2, not_4_out, op0);
  and andi (andi_out, not_1_out, op2, op1, not_3_out);
  and ori (ori_out, not_1_out, op2, op1, op0);
  and bne (bne_out, op3, not_2_out, not_4_out, not_3_out);
  and sw (MemWrite, op3, not_2_out, not_4_out, op0);
  and u_lui (lui_out, op3, not_2_out, op1, not_3_out);
  and lw (lw_out, op3, not_2_out, op1, op0);
  and disp (disp_out, op3, op2, not_4_out, not_3_out);
  or u_RegDST1 (RegDST1, jal_out, 1'b0);
  or u_RegDST0 (RegDST0, jal_out, and_1_out);
  or u_Jump (Jump, jal_out, j_out);
  or u_Branch (Branch, beq_out, 1'b0);
  or u_MemToReg (MemToReg, lw_out, 1'b0);
  or u_signext (signext, beq_out, addi_out, bne_out, MemWrite, lw_out);
  or u_ALUSrc (ALUSrc, addi_out, andi_out, ori_out, MemWrite, lw_out);
  or u_RegWrite (RegWrite, jal_out, addi_out, andi_out, ori_out, lui_out, lw_out, and_1_out);
  or jr_2 (jr, jr_out, 1'b0);
  or Lui_2 (Lui, lui_out, 1'b0);
  or ALUsel0 (ALUsel0_out[0], lw_out, MemWrite, addi_out, andi_out);
  or ALUsel1 (ALUsel0_out[1], ori_out, andi_out);
  Multiplexer #(.select(2), .width(4)) multiplexer_1 (
    .in0(Function[3:0]), .in1(4'b0000), .in2(4'b0110), .in3(4'b0111), .out(ALUSWITCH), .sel(ALUsel0_out));  // open: en
  or u_BranchNE (BranchNE, bne_out, 1'b0);
  or jal_2 (Jal, jal_out, 1'b0);
  or u_Display (display, disp_out, 1'b0);

  // Other names for the same wires on the sheet: func[3:0] = Function[3:0]
endmodule
