// Logisim project alu.circ as structural Verilog: 1 circuit, main circuit main
module main (
  input  [15:0] X,
  input  [15:0] Y,
  input  [3:0] Switch__S,
  output Signed_Overflow,
  output [15:0] RESULT,
  output Equal
);

  wire adder_1_cout, adder_2_cout, adder_3_cout, adder_4_cout, adder_5_cout, adder_6_cout, adder_7_cout,
       adder_9_cout, adder_10_cout, adder_11_cout, adder_12_cout, adder_13_cout, adder_14_cout,
       adder_15_cout, adder_17_cout, adder_18_cout, adder_19_cout, adder_20_cout, adder_21_cout,
       adder_22_cout, adder_23_cout, adder_24_cout, adder_25_cout, adder_26_cout, adder_27_cout,
       adder_28_cout, adder_29_cout, adder_30_cout, adder_31_cout, and_1_out, and_2_out, and_3_out,
       and_4_out, and_6_out, and_7_out, comparator_1_eq, comparator_2_eq, comparator_3_lt, not_1_out,
       not_2_out, not_3_out, not_4_out, not_5_out, not_6_out, not_7_out, not_8_out, not_9_out, or_5_out,
       OverFlow16, OverFlowP8Lower, OverFlowP8upper, select, X0, X1, X2, X3, X4, X5, X6, X7, X8, X9, X10,
       X11, X12, X13, X14, X15, xor_1_out, xor_2_out, xor_3_out, xor_4_out, xor_5_out, xor_6_out, xor_7_out,
       xor_8_out, xor_9_out, xor_10_out, xor_11_out, xor_12_out, xor_13_out, xor_14_out, xor_15_out,
       xor_16_out, xor_17_out, xor_18_out, xor_19_out, xor_20_out, xor_21_out, xor_22_out, xor_23_out,
       xor_24_out, xor_25_out, xor_26_out, xor_27_out, xor_28_out, xor_29_out, xor_30_out, xor_31_out,
       xor_32_out, Y0, Y1, Y2, Y3, Y4, Y5, Y6, Y7, Y8, Y9, Y10, Y11, Y12, Y13, Y14, Y15;
  wire [7:0] adder_1_out, adder_9_out;
  wire [15:0] ADD_out, ADD_X, ADD_Y, adder_17_out, ADDP8_out, ADDP8_X, ADDP8_Y, AND_out, AND_X, AND_Y,
       demultiplexer_1_out2, OR_out, OR_X, OR_Y, SLLV_out, SLLV_X, SLLV_Y, SLT_out, SLT_X, SLT_Y, SRAV_out,
       SRAV_X, SRAV_Y, SRLV_out, SRLV_X, SRLV_Y, SUB_out, SUB_X, SUB_Y, SUBP8_out, SUBP8_X, SUBP8_Y;

  Demultiplexer #(.select(4), .width(16)) demultiplexer_1 (
    .out0(ADD_X), .out1(SUB_X), .out2(demultiplexer_1_out2), .out3(SRLV_X), .out4(SRAV_X), .out5(SLT_X),
    .out6(OR_X), .out7(AND_X), .out8(ADDP8_X), .out9(SUBP8_X), .in(X), .sel(Switch__S));  // open: out10, out11, out12, out13, out14, out15, en
  Demultiplexer #(.select(4), .width(16)) demultiplexer_2 (
    .out0(ADD_Y), .out1(SUB_Y), .out2(SLLV_Y), .out3(SRLV_Y), .out4(SRAV_Y), .out5(SLT_Y), .out6(OR_Y),
    .out7(AND_Y), .out8(ADDP8_Y), .out9(SUBP8_Y), .in(Y), .sel(Switch__S));  // open: out10, out11, out12, out13, out14, out15, en
  Comparator #(.width(4)) comparator_1 (.a(Switch__S), .b(4'b0001), .eq(comparator_1_eq));  // open: gt, lt
  Comparator #(.width(4)) comparator_2 (.a(Switch__S), .b(4'b1001), .eq(comparator_2_eq));  // open: gt, lt
  or or_1 (select, comparator_1_eq, comparator_2_eq);
  not not_1 (not_1_out, X15);
  xor xor_1 (xor_1_out, Y7, select);
  not not_2 (not_2_out, X7);
  xor xor_2 (xor_2_out, Y8, select);
  xor xor_3 (xor_3_out, Y9, select);
  xor xor_4 (xor_4_out, Y10, select);
  xor xor_5 (xor_5_out, Y11, select);
  xor xor_6 (xor_6_out, Y12, select);
  xor xor_7 (xor_7_out, Y13, select);
  xor xor_8 (xor_8_out, Y14, select);
  xor xor_9 (xor_9_out, Y15, select);
  not not_3 (not_3_out, xor_9_out);
  xor xor_10 (xor_10_out, Y0, select);
  xor xor_11 (xor_11_out, Y1, select);
  xor xor_12 (xor_12_out, Y2, select);
  xor xor_13 (xor_13_out, Y3, select);
  xor xor_14 (xor_14_out, Y4, select);
  xor xor_15 (xor_15_out, Y5, select);
  xor xor_16 (xor_16_out, Y6, select);
  not not_4 (not_4_out, xor_1_out);
  Adder #(.width(1)) adder_1 (.a(X0), .b(xor_10_out), .out(adder_1_out[0]), .cin(select), .cout(adder_1_cout));
  Adder #(.width(1)) adder_2 (.a(X1), .b(xor_11_out), .out(adder_1_out[1]), .cin(adder_1_cout), .cout(adder_2_cout));
  Adder #(.width(1)) adder_3 (.a(X2), .b(xor_12_out), .out(adder_1_out[2]), .cin(adder_2_cout), .cout(adder_3_cout));
  Adder #(.width(1)) adder_4 (.a(X3), .b(xor_13_out), .out(adder_1_out[3]), .cin(adder_3_cout), .cout(adder_4_cout));
  Adder #(.width(1)) adder_5 (.a(X4), .b(xor_14_out), .out(adder_1_out[4]), .cin(adder_4_cout), .cout(adder_5_cout));
  Adder #(.width(1)) adder_6 (.a(X5), .b(xor_15_out), .out(adder_1_out[5]), .cin(adder_5_cout), .cout(adder_6_cout));
  Adder #(.width(1)) adder_7 (.a(X6), .b(xor_16_out), .out(adder_1_out[6]), .cin(adder_6_cout), .cout(adder_7_cout));
  Adder #(.width(1)) adder_8 (.a(X7), .b(xor_1_out), .out(adder_1_out[7]), .cin(adder_7_cout));  // open: cout
  not not_5 (not_5_out, adder_1_out[7]);
  Adder #(.width(1)) adder_9 (.a(X8), .b(xor_2_out), .out(adder_9_out[0]), .cin(select), .cout(adder_9_cout));
  Adder #(.width(1)) adder_10 (.a(X9), .b(xor_3_out), .out(adder_9_out[1]), .cin(adder_9_cout), .cout(adder_10_cout));
  Adder #(.width(1)) adder_11 (.a(X10), .b(xor_4_out), .out(adder_9_out[2]), .cin(adder_10_cout), .cout(adder_11_cout));
  Adder #(.width(1)) adder_12 (.a(X11), .b(xor_5_out), .out(adder_9_out[3]), .cin(adder_11_cout), .cout(adder_12_cout));
  Adder #(.width(1)) adder_13 (.a(X12), .b(xor_6_out), .out(adder_9_out[4]), .cin(adder_12_cout), .cout(adder_13_cout));
  Adder #(.width(1)) adder_14 (.a(X13), .b(xor_7_out), .out(adder_9_out[5]), .cin(adder_13_cout), .cout(adder_14_cout));
  Adder #(.width(1)) adder_15 (.a(X14), .b(xor_8_out), .out(adder_9_out[6]), .cin(adder_14_cout), .cout(adder_15_cout));
  Adder #(.width(1)) adder_16 (.a(X15), .b(xor_9_out), .out(adder_9_out[7]), .cin(adder_15_cout));  // open: cout
  not not_6 (not_6_out, adder_9_out[7]);
  and and_1 (and_1_out, not_5_out, xor_1_out, X7);
  and and_2 (and_2_out, adder_1_out[7], not_4_out, not_2_out);
  and and_3 (and_3_out, not_6_out, xor_9_out, X15);
  and and_4 (and_4_out, adder_9_out[7], not_3_out, not_1_out);
  or or_2 (OverFlowP8Lower, and_1_out, and_2_out);
  or or_3 (OverFlowP8upper, and_3_out, and_4_out);
  Shifter #(.width(16)) shifter_1 (.in(SLLV_X), .\dist (SLLV_Y[3:0]), .out(SLLV_out));
  Shifter #(.width(16), .shift("lr")) shifter_2 (.in(SRLV_X), .\dist (SRLV_Y[3:0]), .out(SRLV_out));
  Shifter #(.width(16), .shift("ar")) shifter_3 (.in(SRAV_X), .\dist (SRAV_Y[3:0]), .out(SRAV_out));
  Comparator #(.width(16)) comparator_3 (.a(SLT_X), .b(SLT_Y), .lt(comparator_3_lt));  // open: gt, eq
  assign OR_out = OR_X | OR_Y;  // OR_Gate or_4, 16 bits wide
  assign AND_out = AND_X & AND_Y;  // AND_Gate and_5, 16 bits wide
  assign SLT_out = {{15{1'b0}}, comparator_3_lt};  // Bit_Extender bit_extender_1
  Demultiplexer #(.select(4), .width(16)) demultiplexer_3 (
    .out8(ADDP8_out), .out9(SUBP8_out), .in({adder_9_out, adder_1_out}), .sel(Switch__S));  // open: out0, out1, out2, out3, out4, out5, out6, out7, out10, out11, out12, out13, out14, out15, en
  Multiplexer #(.select(4), .width(16)) multiplexer_1 (
    .in0(ADD_X), .in1(SUB_X), .in8(ADDP8_X), .in9(SUBP8_X),
    .out({X15, X14, X13, X12, X11, X10, X9, X8, X7, X6, X5, X4, X3, X2, X1, X0}), .sel(Switch__S));  // open: in2, in3, in4, in5, in6, in7, in10, in11, in12, in13, in14, in15, en
  Multiplexer #(.select(4), .width(16)) multiplexer_2 (
    .in0(ADD_Y), .in1(SUB_Y), .in8(ADDP8_Y), .in9(SUBP8_Y),
    .out({Y15, Y14, Y13, Y12, Y11, Y10, Y9, Y8, Y7, Y6, Y5, Y4, Y3, Y2, Y1, Y0}), .sel(Switch__S));  // open: in2, in3, in4, in5, in6, in7, in10, in11, in12, in13, in14, in15, en
  or or_5 (or_5_out, OverFlowP8upper, OverFlowP8Lower);
  Multiplexer #(.select(4), .width(16)) multiplexer_3 (
    .in0(ADD_out), .in1(SUB_out), .in2(SLLV_out), .in3(SRLV_out), .in4(SRAV_out), .in5(SLT_out),
    .in6(OR_out), .in7(AND_out), .in8(ADDP8_out), .in9(SUBP8_out), .out(RESULT), .sel(Switch__S));  // open: in10, in11, in12, in13, in14, in15, en
  Comparator #(.width(16)) comparator_4 (.a(X), .b(Y), .eq(Equal));  // open: gt, lt
  Multiplexer #(.select(4)) multiplexer_4 (
    .in0(OverFlow16), .in1(OverFlow16), .in8(or_5_out), .in9(or_5_out), .out(Signed_Overflow), .sel(Switch__S));  // open: in2, in3, in4, in5, in6, in7, in10, in11, in12, in13, in14, in15, en
  xor xor_17 (xor_17_out, Y0, select);
  xor xor_18 (xor_18_out, Y1, select);
  xor xor_19 (xor_19_out, Y2, select);
  xor xor_20 (xor_20_out, Y3, select);
  xor xor_21 (xor_21_out, Y4, select);
  xor xor_22 (xor_22_out, Y5, select);
  xor xor_23 (xor_23_out, Y6, select);
  xor xor_24 (xor_24_out, Y7, select);
  xor xor_25 (xor_25_out, Y8, select);
  xor xor_26 (xor_26_out, Y9, select);
  xor xor_27 (xor_27_out, Y10, select);
  xor xor_28 (xor_28_out, Y11, select);
  xor xor_29 (xor_29_out, Y12, select);
  xor xor_30 (xor_30_out, Y13, select);
  xor xor_31 (xor_31_out, Y14, select);
  xor xor_32 (xor_32_out, Y15, select);
  Adder #(.width(1)) adder_17 (.a(X0), .b(xor_17_out), .out(adder_17_out[0]), .cin(select), .cout(adder_17_cout));
  Adder #(.width(1)) adder_18 (
    .a(X1), .b(xor_18_out), .out(adder_17_out[1]), .cin(adder_17_cout), .cout(adder_18_cout));
  Adder #(.width(1)) adder_19 (
    .a(X2), .b(xor_19_out), .out(adder_17_out[2]), .cin(adder_18_cout), .cout(adder_19_cout));
  Adder #(.width(1)) adder_20 (
    .a(X3), .b(xor_20_out), .out(adder_17_out[3]), .cin(adder_19_cout), .cout(adder_20_cout));
  Adder #(.width(1)) adder_21 (
    .a(X4), .b(xor_21_out), .out(adder_17_out[4]), .cin(adder_20_cout), .cout(adder_21_cout));
  Adder #(.width(1)) adder_22 (
    .a(X5), .b(xor_22_out), .out(adder_17_out[5]), .cin(adder_21_cout), .cout(adder_22_cout));
  Adder #(.width(1)) adder_23 (
    .a(X6), .b(xor_23_out), .out(adder_17_out[6]), .cin(adder_22_cout), .cout(adder_23_cout));
  Adder #(.width(1)) adder_24 (
    .a(X7), .b(xor_24_out), .out(adder_17_out[7]), .cin(adder_23_cout), .cout(adder_24_cout));
  Adder #(.width(1)) adder_25 (
    .a(X8), .b(xor_25_out), .out(adder_17_out[8]), .cin(adder_24_cout), .cout(adder_25_cout));
  Adder #(.width(1)) adder_26 (
    .a(X9), .b(xor_26_out), .out(adder_17_out[9]), .cin(adder_25_cout), .cout(adder_26_cout));
  Adder #(.width(1)) adder_27 (
    .a(X10), .b(xor_27_out), .out(adder_17_out[10]), .cin(adder_26_cout), .cout(adder_27_cout));
  Adder #(.width(1)) adder_28 (
    .a(X11), .b(xor_28_out), .out(adder_17_out[11]), .cin(adder_27_cout), .cout(adder_28_cout));
  Adder #(.width(1)) adder_29 (
    .a(X12), .b(xor_29_out), .out(adder_17_out[12]), .cin(adder_28_cout), .cout(adder_29_cout));
  Adder #(.width(1)) adder_30 (
    .a(X13), .b(xor_30_out), .out(adder_17_out[13]), .cin(adder_29_cout), .cout(adder_30_cout));
  Adder #(.width(1)) adder_31 (
    .a(X14), .b(xor_31_out), .out(adder_17_out[14]), .cin(adder_30_cout), .cout(adder_31_cout));
  Adder #(.width(1)) adder_32 (.a(X15), .b(xor_32_out), .out(adder_17_out[15]), .cin(adder_31_cout));  // open: cout
  not not_7 (not_7_out, adder_17_out[15]);
  not not_8 (not_8_out, xor_32_out);
  not not_9 (not_9_out, X15);
  Demultiplexer #(.select(4), .width(16)) demultiplexer_4 (
    .out0(ADD_out), .out1(SUB_out), .in(adder_17_out), .sel(Switch__S));  // open: out2, out3, out4, out5, out6, out7, out8, out9, out10, out11, out12, out13, out14, out15, en
  and and_6 (and_6_out, not_7_out, xor_32_out, X15);
  and and_7 (and_7_out, adder_17_out[15], not_8_out, not_9_out);
  or or_6 (OverFlow16, and_6_out, and_7_out);

  // Other names for the same wires on the sheet: OverFlow = Signed_Overflow; Switch[3:0] = Switch__S

  // Notes on the sheet:
  //   INPUTS to your circuit
  //   DON'T CHANGE THE INPUTS AND OUTPUTS! IF YOU DO SO, YOU NEED TO MAKE SURE THE PINS ARE IN THE RIGHT PLACES!
  //   OUTPUTS of your circuit
endmodule
